# Fritzing sketch FinalProject (saved by Fritzing 0.9.3b)
breadboards: 3

parts:
  U1 = atmega168 [package=dip]
  IC1 = L293D [package=THT]
  M1 = DC Motor
  LED1 = RGB LED (com. cathode, rbg) [package="5 mm [THT]"]
  LED2 = smd LED [color="Red (633nm)" package="0603 [SMD]"]
  R1 = Resistor [tolerance=±5% resistance=220 package="0805 [SMD]"]
  R2 = Resistor [tolerance=±5% resistance=220 package="0805 [SMD]"]
  U2 = LCD-16X2 [package=lcd-16x2_noholes]
  R3 = Resistor [tolerance=±5% resistance=220 package="0805 [SMD]"]
  R4 = Trimmer Potentiometer [maximum_resistance=10kΩ package=THT]
  VCC1 = 4 x AAA Battery Mount  # not connected
  C1 = Capacitor [package=cap-pth-small]

nets:
  VCC: U1.VCC, U2.VDD, R3.Pin_1, R4.leg2, C1.1
  N1: U1.GND#7, C1.2
  N2: U1.D5_(PWM), U2.RS
  N3: U1.D6_(PWM), U2.R_W
  N4: U1.D7, U2.E
  N5: U1.D8, IC1.Enable_2
  N6: U1.D9_(PWM), IC1.In_3
  N7: U1.D10_(PWM), IC1.In_4
  N8: U1.D11_(PWM), LED1.red_anode
  N9: U1.D12, LED2.anode
  N10: U1.A0, U2.DB7
  N11: U1.A1, U2.DB6
  N12: U1.A2, U2.DB5
  N13: U1.A3, U2.DB4
  N14: IC1.0V, IC1.+V, R1.Pin_0, R2.Pin_0, U2.VSS, U2.K, R4.leg1
  N15: IC1.Out_4_(_Controlled_by_Enable_2_), M1.pin_1
  N16: LED1.blue_anode, R2.Pin_1
  N17: U2.VO, R4.wiper
  N18: U2.A, R3.Pin_0

notes:
  SERIAL IO USB CABLE
  Black: Ground
  Orange: Something controlling something else (OUTPUT)
  Cyan: Driver controlling motor (OUTPTU)
  Green: Enable line
  Purple: DATA for LCD
  Yellow and Orange: Two wires for RX and TX UART communications
  Weather Simulator
  12/1/2017
  Would like to give the LCD its own batter supply, but only have two battery sources, the USART cable and the external power supply.
  The DC motor draws too much power
  Dc Motor
  LCD Screen
  L293D Motor Driver
  RBG LED for cool temperatures
  Red LED for hot temperatures
